// Logisim project Circuito de arquitetura.circ as structural Verilog: 8 circuits, main circuit main
module main (
  input  [1:0] in_1,
  input  [3:0] in_2,
  output [3:0] out_3,
  output [3:0] out_4
);

  Rot_Esq rot_esq_1 (.in_1(in_1), .in_2(in_2), .out_3(out_3));
  Rot_Dir rot_dir_1 (.in_1(in_1), .in_2(in_2), .out_3(out_4));
endmodule

module add_1 (
  input  in_1,
  input  in_2,
  input  in_3,
  output out_4,
  output out_5
);

  wire and_1_out, and_2_out, or_1_out, xor_1_out;

  or or_1 (or_1_out, in_2, in_3);
  xor xor_1 (xor_1_out, in_1, in_2);
  and and_1 (and_1_out, or_1_out, in_1);
  and and_2 (and_2_out, in_2, in_3);
  xor xor_2 (out_4, xor_1_out, in_3);
  or or_2 (out_5, and_1_out, and_2_out);
endmodule

module decodificador_3x8 (
  input  [2:0] in_1,
  output out_2,
  output out_3,
  output out_4,
  output out_5,
  output out_6,
  output out_7,
  output out_8,
  output out_9
);

  wire not_1_out, not_2_out, not_3_out, not_4_out, not_5_out, not_6_out, not_7_out, not_8_out, not_9_out,
       not_10_out, not_11_out, not_12_out;

  not not_1 (not_1_out, in_1[1]);
  not not_2 (not_2_out, in_1[2]);
  not not_3 (not_3_out, in_1[0]);
  not not_4 (not_4_out, in_1[2]);
  not not_5 (not_5_out, in_1[1]);
  not not_6 (not_6_out, in_1[2]);
  not not_7 (not_7_out, in_1[0]);
  not not_8 (not_8_out, in_1[2]);
  not not_9 (not_9_out, in_1[1]);
  not not_10 (not_10_out, in_1[0]);
  not not_11 (not_11_out, in_1[1]);
  not not_12 (not_12_out, in_1[0]);
  and and_1 (out_2, not_2_out, not_1_out, not_3_out);
  and and_2 (out_3, not_4_out, not_5_out, in_1[0]);
  and and_3 (out_4, not_6_out, in_1[1], not_7_out);
  and and_4 (out_5, not_8_out, in_1[1], in_1[0]);
  and and_5 (out_6, in_1[2], not_9_out, not_10_out);
  and and_6 (out_7, in_1[2], not_11_out, in_1[0]);
  and and_7 (out_8, in_1[2], in_1[1], not_12_out);
  and and_8 (out_9, in_1[2], in_1[1], in_1[0]);
endmodule

module buffer (
  input  [3:0] in_1,
  input  in_2,
  output [3:0] out_3
);

  assign out_3[3] = in_2 ? in_1[3] : 1'bz;  // Controlled_Buffer controlled_buffer_1
  assign out_3[2] = in_2 ? in_1[2] : 1'bz;  // Controlled_Buffer controlled_buffer_2
  assign out_3[0] = in_2 ? in_1[0] : 1'bz;  // Controlled_Buffer controlled_buffer_3
  assign out_3[1] = in_2 ? in_1[1] : 1'bz;  // Controlled_Buffer controlled_buffer_4
endmodule

module Add_4 (
  input  [3:0] B,
  input  [3:0] A,
  output Overflow,
  output [3:0] SOMA
);

  wire add_1_1_out_5, add_1_3_out_5, add_1_4_out_5;

  // Probe on A
  add_1 add_1_1 (.out_4(SOMA[2]), .out_5(add_1_1_out_5), .in_1(A[2]), .in_2(B[2]), .in_3(add_1_3_out_5));
  add_1 add_1_2 (.out_4(SOMA[3]), .out_5(Overflow), .in_1(A[3]), .in_2(B[3]), .in_3(add_1_1_out_5));
  add_1 add_1_3 (.out_4(SOMA[1]), .out_5(add_1_3_out_5), .in_1(A[1]), .in_2(B[1]), .in_3(add_1_4_out_5));
  // Probe on SOMA
  add_1 add_1_4 (.out_4(SOMA[0]), .out_5(add_1_4_out_5), .in_1(A[0]), .in_2(B[0]), .in_3(1'b0));
  // Probe on B
endmodule

module _3x8 (
  input  [2:0] in_1,
  output S0,
  output S1,
  output S2,
  output S3,
  output S4,
  output S5,
  output S6,
  output S7
);

  wire not_1_out, not_2_out, not_3_out, not_4_out, not_5_out, not_6_out, not_7_out, not_8_out, not_9_out,
       not_10_out, not_11_out, not_12_out;

  not not_1 (not_1_out, in_1[2]);
  not not_2 (not_2_out, in_1[1]);
  not not_3 (not_3_out, in_1[0]);
  not not_4 (not_4_out, in_1[2]);
  not not_5 (not_5_out, in_1[1]);
  not not_6 (not_6_out, in_1[2]);
  not not_7 (not_7_out, in_1[0]);
  not not_8 (not_8_out, in_1[2]);
  not not_9 (not_9_out, in_1[1]);
  not not_10 (not_10_out, in_1[0]);
  not not_11 (not_11_out, in_1[1]);
  not not_12 (not_12_out, in_1[0]);
  and and_1 (S7, in_1[2], in_1[1], in_1[0]);
  and and_2 (S0, not_1_out, not_2_out, not_3_out);
  and and_3 (S1, not_4_out, not_5_out, in_1[0]);
  and and_4 (S2, not_6_out, in_1[1], not_7_out);
  and and_5 (S3, not_8_out, in_1[1], in_1[0]);
  and and_6 (S4, in_1[2], not_9_out, not_10_out);
  and and_7 (S5, in_1[2], not_11_out, in_1[0]);
  and and_8 (S6, in_1[2], in_1[1], not_12_out);
endmodule

module Rot_Esq (
  input  [1:0] in_1,
  input  [3:0] in_2,
  output [3:0] out_3
);

  wire and_1_out, and_2_out, and_3_out, and_4_out, and_5_out, and_6_out, and_7_out, and_8_out, and_9_out;

  and and_1 (and_1_out, in_2[0], in_1[1], in_1[0]);
  and and_2 (and_2_out, in_2[1], in_1[1], ~in_1[0]);  // AND_Gate
  and and_3 (and_3_out, in_2[2], ~in_1[1], in_1[0]);  // AND_Gate
  and and_4 (and_4_out, in_2[3], ~in_1[1], ~in_1[0]);  // AND_Gate
  and and_5 (and_5_out, in_2[0], in_1[1], ~in_1[0]);  // AND_Gate
  and and_6 (and_6_out, in_2[1], ~in_1[1], in_1[0]);  // AND_Gate
  and and_7 (and_7_out, in_2[2], ~in_1[1], ~in_1[0]);  // AND_Gate
  and and_8 (and_8_out, in_2[0], ~in_1[1], in_1[0]);  // AND_Gate
  and and_9 (and_9_out, in_2[1], ~in_1[1], ~in_1[0]);  // AND_Gate
  and and_10 (out_3[0], in_2[0], ~in_1[1], ~in_1[0]);  // AND_Gate
  or or_1 (out_3[3], and_1_out, and_2_out, and_3_out, and_4_out);
  or or_2 (out_3[2], and_5_out, and_6_out, and_7_out);
  or or_3 (out_3[1], and_8_out, and_9_out);
endmodule

module Rot_Dir (
  input  [1:0] in_1,
  input  [3:0] in_2,
  output [3:0] out_3
);

  wire and_1_out, and_2_out, and_3_out, and_4_out, and_5_out, and_6_out, and_7_out, and_8_out, and_9_out;

  and and_1 (and_1_out, in_2[3], in_1[1], in_1[0]);
  and and_2 (and_2_out, in_2[2], in_1[1], ~in_1[0]);  // AND_Gate
  and and_3 (and_3_out, in_2[1], ~in_1[1], in_1[0]);  // AND_Gate
  and and_4 (and_4_out, in_2[0], ~in_1[1], ~in_1[0]);  // AND_Gate
  and and_5 (and_5_out, in_2[3], in_1[1], ~in_1[0]);  // AND_Gate
  and and_6 (and_6_out, in_2[2], ~in_1[1], in_1[0]);  // AND_Gate
  and and_7 (and_7_out, in_2[1], ~in_1[1], ~in_1[0]);  // AND_Gate
  and and_8 (and_8_out, in_2[3], ~in_1[1], in_1[0]);  // AND_Gate
  and and_9 (and_9_out, in_2[2], ~in_1[1], ~in_1[0]);  // AND_Gate
  and and_10 (out_3[3], in_2[3], ~in_1[1], ~in_1[0]);  // AND_Gate
  or or_1 (out_3[0], and_1_out, and_2_out, and_3_out, and_4_out);
  or or_2 (out_3[1], and_5_out, and_6_out, and_7_out);
  or or_3 (out_3[2], and_8_out, and_9_out);
endmodule
